# Fritzing sketch Zati FYP (saved by Fritzing 0.9.3b)
breadboards: 2

parts:
  Part1 = FC-28 Soil Hygrometer Module
  Part8 = FC-28 Soil Hygrometer Module - Probe
  Mod1 = KY-015 Temperature & Humidity Sensor Module [package="Breakout board"]
  WATER_PUMP1 = water pump/motor  # not connected
  PSU1 = Adjustable Breadboard Power Supply  # not connected
  U4 = 4-Channel 5v Relay Shield [package=relay-4ch5v10a]
  U5 = LuaNode32 / ESP32
  Water_Level_Sensor1 = Water Level Sensor
  WATER_PUMP2 = water pump/motor  # not connected
  WATER_PUMP3 = water pump/motor  # not connected

nets:
  GND: Part1.GND, Water_Level_Sensor1.GND
  N1: Part1.AO, U5.VP
  N2: Part1.POS, Part8.POS
  N3: Part1.NEG, Part8.NEG
  N4: Mod1.S, U5.D25
  N5: U4.VCC, U4.K1-Off, U4.K2-Off, U4.K3-Off
  N6: U4.IN1, U5.D4
  N7: U4.IN2, U5.D2
  N8: U4.IN3, U5.D15
  N9: U5.D35, Water_Level_Sensor1.SIG
  N10: U5.D32, Water_Level_Sensor1.VCC

custom parts:
  FC-28 Soil Hygrometer Module: The FC-28 is a soil hygrometer module that uses the Texas Instruments LM393 comparator chip to provide an analog measurement of soil humidity. The digital output is high when soil moisture is over a certain threshold, as determined by adjusting the potentiometer.
  FC-28 Soil Hygrometer Module - Probe: The FC-28 is a soil hygrometer module that uses the Texas Instruments LM393 comparator chip to provide an analog measurement of soil humidity.
  KY-015 Temperature & Humidity Sensor Module: KY-015 temperature and humidity sensor module, provides a low-latency serial interface to measure humidity and temperature.
  water pump/motor: WATER PUMP BY ARDUBLOCKTR
  4-Channel 5v Relay Shield: 4 Channel 5v Relay Shield w. 2x SPD-06VDC-SD-C
  LuaNode32 / ESP32: ESP32 based LuaNode32
  Water Level Sensor: A water level sensor. This sensor operates at 3V to 5V. The Sig (signal) pin outputs an analogue signal that is in proportion to the amount of water in contact with the sensor.

// code stored in the sketch: Nad Gemok.ino
#define BLYNK_TEMPLATE_ID           "TMPLxxxxxx"
#define BLYNK_DEVICE_NAME           "Device"
#define BLYNK_AUTH_TOKEN            "YourAuthToken"

#define BLYNK_PRINT Serial

#include <ESP8266WiFi.h>        
#include <BlynkSimpleEsp8266.h>
#include <DHT.h>

char auth[] = BLYNK_AUTH_TOKEN;

// Your WiFi credentials.
// Set password to "" for open networks.
char ssid[] = "YourNetworkName";
char pass[] = "YourPassword";

//DHT11 Blynk
#define DHTPIN 4
#define DHTTYPE DHT11

// define the GPIO connected with Relays and switches  
#define RelayPin1 4 //D2
#define SwitchPin1 0 //D3  
#define wifiLed  16  //D0  
#define VPIN_BUTTON_1  V1

int toggleState_1 = 1; //Define integer to remember the toggle state for relay 1
int wifiFlag = 0;  

DHT dht(DHTPIN, DHTTYPE);
BlynkTimer timer;

int sensorpin = A0;  /* Connect Soil moisture analog sensor pin to A0 of NodeMCU */
int sensorvalue=0;
int outputvalue=0;

//DHT11 Sensor Read And Print
void sendSensor()
{
  float h = dht.readHumidity();
  float t = dht.readTemperature(); // or dht.readTemperature(true) for Fahrenheit

  if (isnan(h) || isnan(t)) {
    Serial.println("Failed to read from DHT sensor!");
    return;
  }
  // You can send any value at any time.
  // Please don't send more that 10 values per second.
  Blynk.virtualWrite(V3, h);
  Blynk.virtualWrite(V4, t);
}


void relayOnOff(int relay)
{
	if(toggleState_1 == 1)
	{  
    	digitalWrite(RelayPin1, HIGH); // turn on relay 1  
    	toggleState_1 = 1;  
    	Serial.println("Pump ON");
    }

    else
    {  
    	digitalWrite(RelayPin1, LOW); // turn off relay 1  
        toggleState_1 = 0;  
        Serial.println("Pump OFF");  
    }  
	
	delay(100);
}

void with_internet()
{
   //Manual Switch Control  
   if (digitalRead(SwitchPin1) == LOW)
   {
    	delay(200);  
    	relayOnOff(1);   
    	Blynk.virtualWrite(VPIN_BUTTON_1, toggleState_1);  // Update Button Widget   
   }
}


void without_internet()
{  
   //Manual Switch Control  
   if (digitalRead(SwitchPin1) == LOW)
  	{
    	delay(200);  
    	relayOnOff(1);     
 	}
}


BLYNK_CONNECTED() 
{  
  	// Request the latest state from the server  
  	Blynk.syncVirtual(VPIN_BUTTON_1);
}

// When App button is pushed - switch the state  
BLYNK_WRITE(VPIN_BUTTON_1) 
{
	toggleState_1 = param.asInt();  
	digitalWrite(RelayPin1, toggleState_1);  
}



void checkBlynkStatus() // called every 3 seconds by SimpleTimer
{   
  bool isconnected = Blynk.connected();  
  if (isconnected == false) {  
  wifiFlag = 1;  
  digitalWrite(wifiLed, HIGH); //Turn off WiFi LED  
  }  
  if (isconnected == true) {  
   wifiFlag = 0;  
   digitalWrite(wifiLed, LOW); //Turn on WiFi LED  
  }  
 }


void setup() 
{
	Serial.begin(9600); /* Define baud rate for serial communication */
	pinMode(RelayPin1, OUTPUT);
	pinMode(wifiLed, OUTPUT);  
	pinMode(SwitchPin1, INPUT_PULLUP);
	//During Starting all Relays should TURN OFF  
  	digitalWrite(RelayPin1, toggleState_1);

	Blynk.begin(auth, ssid, pass);
}

void loop() 
{
	//Soil Moisture Sensor Read And Print
	sensorvalue=analogRead(sensorpin);
  	outputvalue=map(sensorvalue,0,1023,0,100); //100,0 pottupaaru
  	delay(1000);

  	if(outputvalue>65)
  	{
       Serial.println("Soil is Wet. Turning Pump Off");
       Serial.print(outputvalue);
       digitalWrite(RelayPin1, HIGH); // turn on relay 1  
       toggleState_1 = 0;
       Blynk.notify("Soil is Wet. Turning Pump Off");
       delay(1000); 
  	}

  	else if(outputvalue<25)
  	{
       Serial.println("Water your Plant. Turning Pump ON");
       Serial.print(outputvalue);
       digitalWrite(RelayPin1, LOW); // turn off relay 1  
       toggleState_1 = 1;
       Blynk.notify("Water your Plant. Turning Pump ON");
       delay(1000);
  	}

  	Blynk.virtualWrite(V2,outputvalue);
  	Blynk.run();

  	if (WiFi.status() != WL_CONNECTED)  
  	{  
   		Serial.println("WiFi Not Connected");  
  	}  
  	else  
  	{  
   		Serial.println("WiFi Connected");  
   		Blynk.run();  
  	}  
  	timer.run(); // Initiates SimpleTimer  
  	if (wifiFlag == 0)  
    	with_internet();  
  	else  
   		without_internet();
}
